// Logisim project Scheme_20_04.circ as structural Verilog: 8 circuits, main circuit main
module main (
  input  Z
);

  wire clock_1_out, D1_q, D2_q, D3_q, D4_q, dtrigger1_1_d1, dtrigger2_1_d1, dtrigger3_1_d1, dtrigger4_1_d1,
       mooreoutput_1_y1, mooreoutput_1_y2, mooreoutput_1_y3, mooreoutput_1_y4, mooreoutput_1_y5,
       mooreoutput_1_y6, mooreoutput_1_y7;

  Clock clock_1 (.out(clock_1_out));
  dTrigger1 dtrigger1_1 (.Q1(D1_q), .Q2(D2_q), .Q3(D3_q), .Q4(D4_q), .Z(Z), .D1(dtrigger1_1_d1));
  dTrigger2 dtrigger2_1 (.Q1(D1_q), .Q2(D2_q), .Q3(D3_q), .Q4(D4_q), .Z(Z), .D1(dtrigger2_1_d1));
  dTrigger3 dtrigger3_1 (.Q1(D1_q), .Q2(D2_q), .Q3(D3_q), .Q4(D4_q), .Z(Z), .D1(dtrigger3_1_d1));
  dTrigger4 dtrigger4_1 (.Q1(D1_q), .Q2(D2_q), .Q3(D3_q), .Q4(D4_q), .Z(Z), .D1(dtrigger4_1_d1));
  D_Flip_Flop D1 (.D(dtrigger1_1_d1), .clk(clock_1_out), .Q(D1_q));  // open: Qn, preset, reset
  D_Flip_Flop D2 (.D(dtrigger2_1_d1), .clk(clock_1_out), .Q(D2_q));  // open: Qn, preset, reset
  D_Flip_Flop D3 (.D(dtrigger3_1_d1), .clk(clock_1_out), .Q(D3_q));  // open: Qn, preset, reset
  D_Flip_Flop D4 (.D(dtrigger4_1_d1), .clk(clock_1_out), .Q(D4_q));  // open: Qn, preset, reset
  MooreOutput mooreoutput_1 (
    .Q1(D1_q), .Q2(D2_q), .Q3(D3_q), .Q4(D4_q), .Y1(mooreoutput_1_y1), .Y2(mooreoutput_1_y2),
    .Y3(mooreoutput_1_y3), .Y4(mooreoutput_1_y4), .Y5(mooreoutput_1_y5), .Y6(mooreoutput_1_y6),
    .Y7(mooreoutput_1_y7));
  _7_Segment_Display u_7_segment_display_1 (
    .g(mooreoutput_1_y7), .f(mooreoutput_1_y6), .a(mooreoutput_1_y1), .b(mooreoutput_1_y2),
    .e(mooreoutput_1_y5), .d(mooreoutput_1_y4), .c(mooreoutput_1_y3));  // open: dp
endmodule

module MooreOutput (
  input  Q1,
  input  Q2,
  input  Q3,
  input  Q4,
  output Y1,
  output Y2,
  output Y3,
  output Y4,
  output Y5,
  output Y6,
  output Y7
);

  wire and_1_out, and_2_out, and_3_out, and_4_out, and_5_out, and_6_out, and_7_out, and_8_out, and_9_out,
       and_10_out, and_11_out, and_12_out, and_13_out, and_14_out, and_15_out, and_16_out, not_1_out,
       not_2_out, not_3_out;

  not not_1 (not_1_out, Q2);
  not not_2 (not_2_out, Q3);
  not not_3 (not_3_out, Q4);
  and and_1 (and_1_out, not_1_out, not_3_out);
  and and_2 (and_2_out, Q2, Q4);
  and and_3 (and_3_out, not_2_out, not_3_out);
  and and_4 (and_4_out, Q3, Q4);
  or or_1 (Y3, not_2_out, Q4, Q2);
  and and_5 (and_5_out, not_1_out, not_3_out);
  and and_6 (and_6_out, not_1_out, Q3);
  and and_7 (and_7_out, Q3, not_3_out);
  and and_8 (and_8_out, Q2, not_2_out, Q4);
  and and_9 (and_9_out, not_1_out, not_3_out);
  and and_10 (and_10_out, Q3, not_3_out);
  and and_11 (and_11_out, not_2_out, not_3_out);
  and and_12 (and_12_out, Q2, not_2_out);
  and and_13 (and_13_out, Q2, not_3_out);
  and and_14 (and_14_out, not_1_out, Q3);
  and and_15 (and_15_out, Q2, not_2_out);
  and and_16 (and_16_out, Q2, not_3_out);
  or or_2 (Y1, and_1_out, Q3, and_2_out, Q1);
  or or_3 (Y2, not_1_out, and_3_out, and_4_out);
  or or_4 (Y4, and_5_out, and_6_out, and_7_out, and_8_out, Q1);
  or or_5 (Y5, and_9_out, and_10_out);
  or or_6 (Y6, and_11_out, and_12_out, and_13_out, Q1);
  or or_7 (Y7, and_14_out, and_15_out, and_16_out, Q1);
endmodule

module dTrigger1 (
  input  Q1,
  input  Q2,
  input  Q3,
  input  Q4,
  input  Z,
  output D1
);

  wire and_1_out, and_2_out, and_3_out, not_1_out, not_2_out, not_3_out, not_4_out, not_5_out;

  not not_1 (not_1_out, Q1);
  not not_2 (not_2_out, Q2);
  not not_3 (not_3_out, Q3);
  not not_4 (not_4_out, Q4);
  not not_5 (not_5_out, Z);
  and and_1 (and_1_out, not_1_out, Q2, Q3, Q4, Z);
  and and_2 (and_2_out, Q1, not_2_out, not_3_out, not_4_out);
  and and_3 (and_3_out, Q1, not_2_out, not_3_out, not_5_out);
  or or_1 (D1, and_1_out, and_2_out, and_3_out);
endmodule

module dTrigger2 (
  input  Q1,
  input  Q2,
  input  Q3,
  input  Q4,
  input  Z,
  output D1
);

  wire and_1_out, and_2_out, and_3_out, and_4_out, not_1_out, not_2_out, not_3_out, not_4_out, not_5_out;

  not not_1 (not_1_out, Q1);
  not not_2 (not_2_out, Q2);
  not not_3 (not_3_out, Q3);
  not not_4 (not_4_out, Q4);
  not not_5 (not_5_out, Z);
  and and_1 (and_1_out, not_1_out, not_2_out, Q3, Q4, Z);
  and and_2 (and_2_out, not_1_out, Q2, not_3_out);
  and and_3 (and_3_out, not_1_out, Q2, not_4_out);
  and and_4 (and_4_out, not_1_out, Q2, not_5_out);
  or or_1 (D1, and_1_out, and_2_out, and_3_out, and_4_out);
endmodule

module dTrigger3 (
  input  Q1,
  input  Q2,
  input  Q3,
  input  Q4,
  input  Z,
  output D1
);

  wire and_1_out, and_2_out, and_3_out, not_1_out, not_2_out, not_3_out, not_4_out;

  not not_1 (not_1_out, Q1);
  not not_2 (not_2_out, Q3);
  not not_3 (not_3_out, Q4);
  not not_4 (not_4_out, Z);
  and and_1 (and_1_out, not_1_out, not_2_out, Q4, Z);
  and and_2 (and_2_out, not_1_out, Q3, not_3_out);
  and and_3 (and_3_out, not_1_out, Q3, not_4_out);
  or or_1 (D1, and_1_out, and_2_out, and_3_out);
endmodule

module dTrigger4 (
  input  Q1,
  input  Q2,
  input  Q3,
  input  Q4,
  input  Z,
  output D1
);

  wire and_1_out, and_2_out, and_3_out, and_4_out, not_1_out, not_2_out, not_3_out, not_4_out, not_5_out;

  not not_1 (not_1_out, Q1);
  not not_2 (not_2_out, Q2);
  not not_3 (not_3_out, Q3);
  not not_4 (not_4_out, Q4);
  not not_5 (not_5_out, Z);
  and and_1 (and_1_out, not_1_out, not_4_out, Z);
  and and_2 (and_2_out, not_2_out, not_3_out, not_4_out, Z);
  and and_3 (and_3_out, not_1_out, Q4, not_5_out);
  and and_4 (and_4_out, not_2_out, not_3_out, Q4, not_5_out);
  or or_1 (D1, and_1_out, and_2_out, and_3_out, and_4_out);
endmodule

module production (
  input  Z
);

  wire and_1_out, and_2_out, and_3_out, and_4_out, and_5_out, and_6_out, and_7_out, and_8_out, and_9_out,
       and_10_out, and_11_out, and_12_out, and_13_out, and_14_out, and_15_out, and_16_out, and_17_out,
       and_18_out, and_19_out, and_20_out, and_21_out, and_22_out, and_23_out, and_24_out, and_25_out,
       and_26_out, and_27_out, and_28_out, and_29_out, and_30_out, clock_1_out, D1_q, D1_qn, D2_q, D2_qn,
       D3_q, D3_qn, D4_q, D4_qn, not_1_out, or_1_out, or_2_out, or_3_out, or_4_out, or_5_out, or_6_out,
       or_7_out, or_8_out, or_9_out, or_10_out, or_11_out;

  not not_1 (not_1_out, Z);
  and and_1 (and_1_out, D1_qn, D2_q, D3_q, D4_q, Z);
  and and_2 (and_2_out, D1_q, D2_qn, D3_qn, D4_qn);
  or or_1 (or_1_out, and_1_out, and_2_out, and_3_out);
  and and_3 (and_3_out, D1_q, D2_qn, D3_qn, not_1_out);
  and and_4 (and_4_out, D1_qn, D2_qn, D3_q, D4_q, Z);
  and and_5 (and_5_out, D1_qn, D2_q, D3_qn);
  and and_6 (and_6_out, D1_qn, D2_q, D4_qn);
  and and_7 (and_7_out, D1_qn, D2_q, not_1_out);
  and and_8 (and_8_out, D1_qn, D3_qn, D4_q, Z);
  and and_9 (and_9_out, D1_qn, D3_q, D4_qn);
  or or_2 (or_2_out, and_8_out, and_9_out, and_10_out);
  and and_10 (and_10_out, D1_qn, D3_q, not_1_out);
  and and_11 (and_11_out, D1_qn, D4_qn, Z);
  and and_12 (and_12_out, D2_qn, D3_qn, D4_qn, Z);
  and and_13 (and_13_out, D1_qn, D4_q, not_1_out);
  and and_14 (and_14_out, D2_qn, D3_qn, D4_q, not_1_out);
  Clock clock_1 (.out(clock_1_out));
  or or_3 (or_3_out, and_4_out, and_5_out, and_6_out, and_7_out);
  or or_4 (or_4_out, and_11_out, and_12_out, and_13_out, and_14_out);
  D_Flip_Flop D1 (.D(or_1_out), .clk(clock_1_out), .Q(D1_q), .Qn(D1_qn));  // open: preset, reset
  D_Flip_Flop D2 (.D(or_3_out), .clk(clock_1_out), .Q(D2_q), .Qn(D2_qn));  // open: preset, reset
  D_Flip_Flop D3 (.D(or_2_out), .clk(clock_1_out), .Q(D3_q), .Qn(D3_qn));  // open: preset, reset
  D_Flip_Flop D4 (.D(or_4_out), .clk(clock_1_out), .Q(D4_q), .Qn(D4_qn));  // open: preset, reset
  and and_15 (and_15_out, D2_qn, D4_qn);
  and and_16 (and_16_out, D2_q, D4_q);
  and and_17 (and_17_out, D3_qn, D4_qn);
  and and_18 (and_18_out, D3_q, D4_q);
  or or_5 (or_5_out, D3_qn, D4_q, D2_q);
  and and_19 (and_19_out, D2_qn, D4_qn);
  and and_20 (and_20_out, D2_qn, D3_q);
  and and_21 (and_21_out, D3_q, D4_qn);
  and and_22 (and_22_out, D2_q, D3_qn, D4_q);
  and and_23 (and_23_out, D2_qn, D4_qn);
  and and_24 (and_24_out, D3_q, D4_qn);
  and and_25 (and_25_out, D3_qn, D4_qn);
  and and_26 (and_26_out, D2_q, D3_qn);
  and and_27 (and_27_out, D2_q, D4_qn);
  and and_28 (and_28_out, D2_qn, D3_q);
  and and_29 (and_29_out, D2_q, D3_qn);
  and and_30 (and_30_out, D2_q, D4_qn);
  or or_6 (or_6_out, and_15_out, D3_q, and_16_out, D1_q);
  or or_7 (or_7_out, D2_qn, and_17_out, and_18_out);
  or or_8 (or_8_out, and_19_out, and_20_out, and_21_out, and_22_out, D1_q);
  or or_9 (or_9_out, and_23_out, and_24_out);
  or or_10 (or_10_out, and_25_out, and_26_out, and_27_out, D1_q);
  or or_11 (or_11_out, and_28_out, and_29_out, and_30_out, D1_q);
  _7_Segment_Display u_7_segment_display_1 (
    .g(or_11_out), .f(or_10_out), .a(or_6_out), .b(or_7_out), .e(or_9_out), .d(or_8_out), .c(or_5_out));  // open: dp
endmodule

module productionBus (
  input  Z
);

  wire and_1_out, and_2_out, and_3_out, and_4_out, and_5_out, and_6_out, and_7_out, and_8_out, and_9_out,
       and_10_out, and_11_out, and_12_out, and_13_out, and_14_out, and_15_out, and_16_out, and_17_out,
       and_18_out, and_19_out, and_20_out, and_21_out, and_22_out, and_23_out, and_24_out, and_25_out,
       and_26_out, and_27_out, and_28_out, and_29_out, and_30_out, clock_1_out, D1_q, D1_qn, D2_q, D2_qn,
       D3_q, D3_qn, D4_q, D4_qn, not_1_out, or_1_out, or_2_out, or_3_out, or_4_out, or_5_out, or_6_out,
       or_7_out, or_8_out, or_9_out, or_10_out, or_11_out;

  not not_1 (not_1_out, Z);
  and and_1 (and_1_out, D1_qn, D2_q, D3_q, D4_q, Z);
  and and_2 (and_2_out, D1_q, D2_qn, D3_qn, D4_qn);
  or or_1 (or_1_out, and_1_out, and_2_out, and_3_out);
  and and_3 (and_3_out, D1_q, D2_qn, D3_qn, not_1_out);
  and and_4 (and_4_out, D1_qn, D2_qn, D3_q, D4_q, Z);
  and and_5 (and_5_out, D1_qn, D2_q, D3_qn);
  and and_6 (and_6_out, D1_qn, D2_q, D4_qn);
  and and_7 (and_7_out, D1_qn, D2_q, not_1_out);
  and and_8 (and_8_out, D1_qn, D3_qn, D4_q, Z);
  and and_9 (and_9_out, D1_qn, D3_q, D4_qn);
  or or_2 (or_2_out, and_8_out, and_9_out, and_10_out);
  and and_10 (and_10_out, D1_qn, D3_q, not_1_out);
  and and_11 (and_11_out, D1_qn, D4_qn, Z);
  and and_12 (and_12_out, D2_qn, D3_qn, D4_qn, Z);
  and and_13 (and_13_out, D1_qn, D4_q, not_1_out);
  and and_14 (and_14_out, D2_qn, D3_qn, D4_q, not_1_out);
  Clock clock_1 (.out(clock_1_out));
  or or_3 (or_3_out, and_4_out, and_5_out, and_6_out, and_7_out);
  or or_4 (or_4_out, and_11_out, and_12_out, and_13_out, and_14_out);
  D_Flip_Flop D1 (.D(or_1_out), .clk(clock_1_out), .Q(D1_q), .Qn(D1_qn));  // open: preset, reset
  D_Flip_Flop D2 (.D(or_3_out), .clk(clock_1_out), .Q(D2_q), .Qn(D2_qn));  // open: preset, reset
  D_Flip_Flop D3 (.D(or_2_out), .clk(clock_1_out), .Q(D3_q), .Qn(D3_qn));  // open: preset, reset
  D_Flip_Flop D4 (.D(or_4_out), .clk(clock_1_out), .Q(D4_q), .Qn(D4_qn));  // open: preset, reset
  and and_15 (and_15_out, D2_qn, D4_qn);
  and and_16 (and_16_out, D2_q, D4_q);
  and and_17 (and_17_out, D3_qn, D4_qn);
  and and_18 (and_18_out, D3_q, D4_q);
  or or_5 (or_5_out, D3_qn, D4_q, D2_q);
  and and_19 (and_19_out, D2_qn, D4_qn);
  and and_20 (and_20_out, D2_qn, D3_q);
  and and_21 (and_21_out, D3_q, D4_qn);
  and and_22 (and_22_out, D2_q, D3_qn, D4_q);
  and and_23 (and_23_out, D2_qn, D4_qn);
  and and_24 (and_24_out, D3_q, D4_qn);
  and and_25 (and_25_out, D3_qn, D4_qn);
  and and_26 (and_26_out, D2_q, D3_qn);
  and and_27 (and_27_out, D2_q, D4_qn);
  and and_28 (and_28_out, D2_qn, D3_q);
  and and_29 (and_29_out, D2_q, D3_qn);
  and and_30 (and_30_out, D2_q, D4_qn);
  or or_6 (or_6_out, and_15_out, D3_q, and_16_out, D1_q);
  or or_7 (or_7_out, D2_qn, and_17_out, and_18_out);
  or or_8 (or_8_out, and_19_out, and_20_out, and_21_out, and_22_out, D1_q);
  or or_9 (or_9_out, and_23_out, and_24_out);
  or or_10 (or_10_out, and_25_out, and_26_out, and_27_out, D1_q);
  or or_11 (or_11_out, and_28_out, and_29_out, and_30_out, D1_q);
  _7_Segment_Display u_7_segment_display_1 (
    .g(or_11_out), .f(or_10_out), .a(or_6_out), .b(or_7_out), .e(or_9_out), .d(or_8_out), .c(or_5_out));  // open: dp
endmodule
