// Logisim project Scheme_20_04_Letters.circ as structural Verilog: 3 circuits, main circuit outputLogic
module outputLogic (
  input  Q1,
  input  Q2,
  input  Q3,
  input  Q4,
  output Y1,
  output Y2,
  output Y3,
  output Y4,
  output Y5,
  output Y6,
  output Y7
);

  wire and_1_out, and_2_out, and_3_out, and_4_out, and_5_out, and_6_out, and_7_out, and_8_out, and_9_out,
       and_10_out, and_11_out, and_12_out, and_13_out, and_14_out, and_15_out, and_16_out, and_17_out,
       and_18_out, and_19_out, and_20_out, and_21_out, and_22_out, and_23_out, and_24_out, and_25_out,
       and_26_out, and_27_out, and_28_out, and_29_out, and_30_out, and_31_out, and_32_out, and_33_out,
       and_34_out, and_35_out, and_36_out, not_1_out, not_2_out, not_3_out, not_4_out;

  not not_1 (not_1_out, Q1);
  not not_2 (not_2_out, Q2);
  not not_3 (not_3_out, Q3);
  not not_4 (not_4_out, Q4);
  and and_1 (and_1_out, not_2_out, not_4_out);
  and and_2 (and_2_out, not_1_out, Q3);
  and and_3 (and_3_out, not_1_out, Q2, Q4);
  and and_4 (and_4_out, Q2, Q3);
  and and_5 (and_5_out, Q1, not_2_out, not_3_out);
  and and_6 (and_6_out, Q1, not_4_out);
  and and_7 (and_7_out, not_1_out, not_2_out);
  and and_8 (and_8_out, not_1_out, not_3_out, not_4_out);
  and and_9 (and_9_out, not_2_out, not_4_out);
  and and_10 (and_10_out, not_1_out, Q3, Q4);
  and and_11 (and_11_out, Q1, not_3_out, Q4);
  and and_12 (and_12_out, not_1_out, not_3_out);
  and and_13 (and_13_out, not_1_out, Q4);
  and and_14 (and_14_out, not_3_out, Q4);
  and and_15 (and_15_out, not_1_out, Q2);
  and and_16 (and_16_out, Q1, not_2_out);
  and and_17 (and_17_out, not_1_out, not_2_out, not_4_out);
  and and_18 (and_18_out, not_1_out, Q3, not_4_out);
  and and_19 (and_19_out, not_2_out, Q3, Q4);
  and and_20 (and_20_out, Q2, not_3_out, Q4);
  and and_21 (and_21_out, Q1, not_3_out);
  and and_22 (and_22_out, Q1, Q2, not_4_out);
  and and_23 (and_23_out, not_2_out, not_4_out);
  and and_24 (and_24_out, Q3, not_4_out);
  and and_25 (and_25_out, Q1, Q3);
  and and_26 (and_26_out, Q1, Q2);
  and and_27 (and_27_out, not_3_out, not_4_out);
  and and_28 (and_28_out, not_1_out, Q2, not_3_out);
  and and_29 (and_29_out, Q2, not_4_out);
  and and_30 (and_30_out, Q1, not_2_out);
  and and_31 (and_31_out, Q1, Q3);
  and and_32 (and_32_out, not_2_out, Q3);
  and and_33 (and_33_out, Q3, not_4_out);
  and and_34 (and_34_out, not_1_out, Q2, not_3_out);
  and and_35 (and_35_out, Q1, not_2_out);
  and and_36 (and_36_out, Q1, Q4);
  or or_1 (Y1, and_1_out, and_2_out, and_3_out, and_4_out, and_5_out, and_6_out);
  or or_2 (Y2, and_7_out, and_8_out, and_9_out, and_10_out, and_11_out);
  or or_3 (Y3, and_12_out, and_13_out, and_14_out, and_15_out, and_16_out);
  or or_4 (Y4, and_17_out, and_18_out, and_19_out, and_20_out, and_21_out, and_22_out);
  or or_5 (Y5, and_23_out, and_24_out, and_25_out, and_26_out);
  or or_6 (Y6, and_27_out, and_28_out, and_29_out, and_30_out, and_31_out);
  or or_7 (Y7, and_32_out, and_33_out, and_34_out, and_35_out, and_36_out);
endmodule

module tLogic (
  input  Z
);

  wire and_1_out, and_2_out, and_3_out, and_4_out, and_5_out, and_6_out, and_7_out, and_8_out, and_9_out,
       and_10_out, and_11_out, and_12_out, and_13_out, and_14_out, and_15_out, and_16_out, and_17_out,
       and_18_out, and_19_out, and_20_out, and_21_out, and_22_out, and_23_out, and_24_out, and_25_out,
       and_26_out, and_27_out, and_28_out, and_29_out, and_30_out, and_31_out, and_32_out, and_33_out,
       and_34_out, and_35_out, and_36_out, and_37_out, and_38_out, and_39_out, and_40_out, and_41_out,
       and_42_out, and_43_out, and_44_out, and_45_out, and_46_out, and_47_out, and_48_out, and_49_out,
       and_50_out, clock_1_out, D1_q, D1_qn, D2_q, D2_qn, D3_q, D3_qn, D4_q, D4_qn, not_1_out, or_1_out,
       or_2_out, or_3_out, or_4_out, or_5_out, or_6_out, or_7_out, or_8_out, or_9_out, or_10_out, or_11_out;

  Clock clock_1 (.out(clock_1_out));
  not not_1 (not_1_out, Z);
  and and_1 (and_1_out, D1_qn, D2_q, D3_q, D4_q, Z);
  and and_2 (and_2_out, D1_q, D2_qn);
  and and_3 (and_3_out, D1_q, D3_qn);
  and and_4 (and_4_out, D1_q, D4_qn);
  and and_5 (and_5_out, D1_q, not_1_out);
  and and_6 (and_6_out, D2_qn, D3_q, D4_q, Z);
  and and_7 (and_7_out, D2_q, D3_qn);
  and and_8 (and_8_out, D2_q, D4_qn);
  and and_9 (and_9_out, D2_q, not_1_out);
  and and_10 (and_10_out, D3_qn, D4_q, Z);
  and and_11 (and_11_out, D3_q, D4_qn);
  and and_12 (and_12_out, D3_q, not_1_out);
  and and_13 (and_13_out, D4_qn, Z);
  and and_14 (and_14_out, D4_q, not_1_out);
  or or_1 (or_1_out, and_1_out, and_2_out, and_3_out, and_4_out, and_5_out);
  or or_2 (or_2_out, and_6_out, and_7_out, and_8_out, and_9_out);
  or or_3 (or_3_out, and_10_out, and_11_out, and_12_out);
  or or_4 (or_4_out, and_13_out, and_14_out);
  D_Flip_Flop D1 (.D(or_1_out), .clk(clock_1_out), .Q(D1_q), .Qn(D1_qn));  // open: preset, reset
  D_Flip_Flop D2 (.D(or_2_out), .clk(clock_1_out), .Q(D2_q), .Qn(D2_qn));  // open: preset, reset
  D_Flip_Flop D3 (.D(or_3_out), .clk(clock_1_out), .Q(D3_q), .Qn(D3_qn));  // open: preset, reset
  D_Flip_Flop D4 (.D(or_4_out), .clk(clock_1_out), .Q(D4_q), .Qn(D4_qn));  // open: preset, reset
  and and_15 (and_15_out, D2_qn, D4_qn);
  and and_16 (and_16_out, D1_qn, D3_q);
  and and_17 (and_17_out, D1_qn, D2_q, D4_q);
  and and_18 (and_18_out, D2_q, D3_q);
  and and_19 (and_19_out, D1_q, D2_qn, D3_qn);
  and and_20 (and_20_out, D1_q, D4_qn);
  and and_21 (and_21_out, D1_qn, D2_qn);
  and and_22 (and_22_out, D1_qn, D3_qn, D4_qn);
  and and_23 (and_23_out, D2_qn, D4_qn);
  and and_24 (and_24_out, D1_qn, D3_q, D4_q);
  and and_25 (and_25_out, D1_q, D3_qn, D4_q);
  and and_26 (and_26_out, D1_qn, D3_qn);
  and and_27 (and_27_out, D1_qn, D4_q);
  and and_28 (and_28_out, D3_qn, D4_q);
  and and_29 (and_29_out, D1_qn, D2_q);
  and and_30 (and_30_out, D1_q, D2_qn);
  and and_31 (and_31_out, D1_qn, D2_qn, D4_qn);
  and and_32 (and_32_out, D1_qn, D3_q, D4_qn);
  and and_33 (and_33_out, D2_qn, D3_q, D4_q);
  and and_34 (and_34_out, D2_q, D3_qn, D4_q);
  and and_35 (and_35_out, D1_q, D3_qn);
  and and_36 (and_36_out, D1_q, D2_q, D4_qn);
  and and_37 (and_37_out, D2_qn, D4_qn);
  and and_38 (and_38_out, D3_q, D4_qn);
  and and_39 (and_39_out, D1_q, D3_q);
  and and_40 (and_40_out, D1_q, D2_q);
  and and_41 (and_41_out, D3_qn, D4_qn);
  and and_42 (and_42_out, D1_qn, D2_q, D3_qn);
  and and_43 (and_43_out, D2_q, D4_qn);
  and and_44 (and_44_out, D1_q, D2_qn);
  and and_45 (and_45_out, D1_q, D3_q);
  and and_46 (and_46_out, D2_qn, D3_q);
  and and_47 (and_47_out, D3_q, D4_qn);
  and and_48 (and_48_out, D1_qn, D2_q, D3_qn);
  and and_49 (and_49_out, D1_q, D2_qn);
  and and_50 (and_50_out, D1_q, D4_q);
  or or_5 (or_5_out, and_15_out, and_16_out, and_17_out, and_18_out, and_19_out, and_20_out);
  or or_6 (or_6_out, and_21_out, and_22_out, and_23_out, and_24_out, and_25_out);
  or or_7 (or_7_out, and_26_out, and_27_out, and_28_out, and_29_out, and_30_out);
  or or_8 (or_8_out, and_31_out, and_32_out, and_33_out, and_34_out, and_35_out, and_36_out);
  or or_9 (or_9_out, and_37_out, and_38_out, and_39_out, and_40_out);
  or or_10 (or_10_out, and_41_out, and_42_out, and_43_out, and_44_out, and_45_out);
  or or_11 (or_11_out, and_46_out, and_47_out, and_48_out, and_49_out, and_50_out);
  _7_Segment_Display u_7_segment_display_1 (
    .g(or_11_out), .f(or_10_out), .a(or_5_out), .b(or_6_out), .e(or_9_out), .d(or_8_out), .c(or_7_out));  // open: dp
endmodule

module display_test (
  input  in_1,
  input  in_2,
  input  in_3,
  input  in_4,
  input  in_5,
  input  in_6,
  input  in_7
);

  _7_Segment_Display u_7_segment_display_1 (
    .g(in_7), .f(in_6), .a(in_1), .b(in_2), .e(in_5), .d(in_4), .c(in_3));  // open: dp
endmodule
