// Logisim project Encryptor.circ as structural Verilog: 1 circuit, main circuit main
module main (
  input  X1,
  input  X2,
  input  X3,
  input  X4,
  input  X5,
  output Y2,
  output Y1,
  output Y0
);

  wire and_1_out, and_2_out, and_3_out, and_4_out, and_5_out, not_1_out, not_2_out, not_3_out, not_4_out,
       not_5_out;

  not not_1 (not_1_out, X1);
  not not_2 (not_2_out, X2);
  not not_3 (not_3_out, X3);
  not not_4 (not_4_out, X4);
  not not_5 (not_5_out, X5);
  and and_1 (and_1_out, not_1_out, not_2_out, not_3_out, X4, not_5_out);
  and and_2 (and_2_out, X3, not_4_out, not_5_out);
  and and_3 (and_3_out, X2, not_4_out, not_5_out);
  and and_4 (and_4_out, X3, not_4_out);
  and and_5 (and_5_out, X1, not_2_out, not_4_out);
  or or_1 (Y2, X4, X5);
  LED led_1 (.in(Y2));
  or or_2 (Y1, and_1_out, and_2_out, and_3_out);
  LED led_2 (.in(Y1));
  or or_3 (Y0, X5, and_4_out, and_5_out);
  LED led_3 (.in(Y0));

  // Notes on the sheet:
  //   Y2 = X5+X4 
  //   Y0 = x5 + x3x4' + x1x2'x4'
  //   Y1 = x1'x2'x3'x4x5' + x3x4'x5' + x2x4'x5'
endmodule
