// Logisim project Task_5.circ as structural Verilog: 5 circuits, main circuit main
module main (
  output Y1,
  output Y2
);

  wire and_1_out, button_1_out, clock_1_out, T1_qn, T2_q;

  Button button_1 (.out(button_1_out));
  Clock clock_1 (.out(clock_1_out));
  T_Flip_Flop T1 (.T(button_1_out), .clk(clock_1_out), .Q(Y1), .Qn(T1_qn));  // open: reset, preset
  T_Flip_Flop T2 (.T(and_1_out), .clk(clock_1_out), .Q(T2_q));  // open: Qn, reset, preset
  and and_1 (and_1_out, T1_qn, button_1_out);
  and and_2 (Y2, T1_qn, T2_q);
endmodule

module main_v2 (
  input  Z,
  output Y2,
  output Y1
);

  wire and_1_out, and_2_out, and_3_out, and_4_out, and_5_out, clock_1_out, D1_qn, D2_qn, not_1_out, or_1_out,
       or_2_out;

  Clock clock_1 (.out(clock_1_out));
  not not_1 (not_1_out, Z);
  and and_1 (and_1_out, D1_qn, Z);
  and and_2 (and_2_out, Y2, not_1_out);
  and and_3 (and_3_out, D1_qn, D2_qn, Z);
  and and_4 (and_4_out, Y1, not_1_out);
  and and_5 (and_5_out, Y2, Y1);
  or or_1 (or_1_out, and_1_out, and_2_out);
  or or_2 (or_2_out, and_3_out, and_4_out, and_5_out);
  D_Flip_Flop D1 (.D(or_1_out), .clk(clock_1_out), .Q(Y2), .Qn(D1_qn));  // open: preset, reset
  D_Flip_Flop D2 (.D(or_2_out), .clk(clock_1_out), .Q(Y1), .Qn(D2_qn));  // open: preset, reset
endmodule

module main_v3 (
  input  Z,
  output Y1,
  output Y2,
  output Y3,
  output Y4
);

  wire and_1_out, and_2_out, and_3_out, and_4_out, and_5_out, clock_1_out, D1_qn, D2_q, D2_qn, not_1_out,
       or_1_out, or_2_out;

  Clock clock_1 (.out(clock_1_out));
  not not_1 (not_1_out, Z);
  and and_1 (and_1_out, D1_qn, Z);
  and and_2 (and_2_out, Y3, not_1_out);
  and and_3 (and_3_out, D1_qn, D2_qn, Z);
  and and_4 (and_4_out, D2_q, not_1_out);
  and and_5 (and_5_out, Y3, D2_q);
  or or_1 (or_1_out, and_1_out, and_2_out);
  or or_2 (or_2_out, and_3_out, and_4_out, and_5_out);
  D_Flip_Flop D1 (.D(or_1_out), .clk(clock_1_out), .Q(Y3), .Qn(D1_qn));  // open: preset, reset
  D_Flip_Flop D2 (.D(or_2_out), .clk(clock_1_out), .Q(D2_q), .Qn(D2_qn));  // open: preset, reset
  and and_6 (Y2, D1_qn, D2_q);
  and and_7 (Y4, Y3, D2_q);

  assign Y1 = 1'b0;
endmodule

module outLogic (
  input  Q1,
  input  Q2,
  output Y1,
  output Y2
);


  assign Y1 = Q1;
  assign Y2 = Q2;
endmodule

module outLogic2 (
  input  Q1,
  input  Q2,
  output Y1,
  output Y2,
  output Y3,
  output Y4
);

  wire not_1_out;

  not not_1 (not_1_out, Q1);
  and and_1 (Y2, not_1_out, Q2);
  and and_2 (Y4, Q1, Q2);

  assign Y1 = 1'b0;
  assign Y3 = Q1;
endmodule
